# Fritzing sketch fritzing (saved by Fritzing 0.9.3b)

parts:
  Bauteil1 = Arduino Nano (Rev3.0)
  Raspberry_Pi_1 = Raspberry Pi 3 [part_number=RPI-3-V1.2]
  Bauteil3 = Logic Level Converter
  Bauteil4 = NeoPixel NeoMatrix 8x8 [part_number=1487]
  Bauteil5 = Arduino Nano (Rev3.0)
  Bauteil6 = NeoPixel NeoMatrix 8x8 [part_number=1487]

nets:
  GND: Bauteil1.GND, Raspberry_Pi_1.GND, Bauteil3.GND, Bauteil4.GND, Bauteil5.GND, Bauteil6.GND
  5V: Bauteil1.D3, Bauteil1.5V, Bauteil3.HV, Bauteil3.RX2_HV, Bauteil4.VDD, Bauteil5.5V, Bauteil6.VDD
  N1: Bauteil1.D6, Bauteil4.IN
  N2: Bauteil1.A5, Bauteil3.RX_HV, Bauteil5.A5
  N3: Bauteil1.A4, Bauteil1.A3, Bauteil3.TX_HV, Bauteil5.A4
  N4: Raspberry_Pi_1.3v3, Bauteil3.LV
  N5: Raspberry_Pi_1.GPIO2, Bauteil3.TX_LV
  N6: Raspberry_Pi_1.GPIO3, Bauteil3.RX_LV
  N7: Bauteil5.D6, Bauteil6.IN

custom parts:
  NeoPixel NeoMatrix 8x8: Put on your sunglasses before wiring up this LED matrix - 64 eye-blistering RGB LEDs adorn the NeoMatrix for a blast of configurable color. Arranged in an 8x8 matrix, each pixel is individually addressable. Only one microcontroller pin is required to control all the LEDs, and you get 24 bit color for each LED.
